# Fritzing sketch RF24SN-example-C_range_tester (saved by Fritzing 0.9.0b)
circuit board: 8.46667cm x 5.64444cm
breadboards: 1

parts:
  Part1 = Arduino Uno (Rev3)
  NRF24L1 = NRF24L01
  R1 = Resistor [tolerance=±5% resistance=1k package=THT]
  R3 = Resistor [tolerance=±5% resistance=1k package=THT]
  R4 = Resistor [tolerance=±5% resistance=1k package=THT]
  LED1 = RGB LED (com. cathode, rbg) [package="5 mm [THT]"]

nets:
  N1: Part1.D9_PWM, NRF24L1.CE
  N2: Part1.D10_PWM/SS, NRF24L1.CSN
  N3: Part1.D11_PWM/MOSI, NRF24L1.MOSI
  N4: Part1.D12/MISO, NRF24L1.MISO
  N5: Part1.D13/SCK, NRF24L1.SCK
  N6: Part1.D5_PWM, R3.Pin_1
  N7: Part1.D6_PWM, R4.Pin_1
  N8: Part1.D7, R1.Pin_1
  3V3: Part1.3V3, NRF24L1.VCC
  GND: Part1.GND, NRF24L1.GND, LED1.common_cathode
  N9: R1.Pin_0, LED1.green_anode
  N10: R3.Pin_0, LED1.red_anode
  N11: R4.Pin_0, LED1.blue_anode

custom parts:
  NRF24L01: NRF24L01 module
